# Fritzing sketch emf_amplifier (saved by Fritzing 0.9.0b)
circuit board: 2.88818cm x 2.54362cm
breadboards: 1

parts:
  LM386 = LM386 [package=dip08]
  C2 = Electrolytic Capacitor [capacitance=250µF package="100 mil [THT, electrolytic]"]
  C3 = Electrolytic Capacitor [capacitance=10µF package="100 mil [THT, electrolytic]"]
  R2 = Resistor [tolerance=±5% resistance=10 package=THT]
  V1 = DC Power [voltage=5]
  C5 = Tantalum Capacitor [capacitance=0.1µF package="100 mil [THT, tantalum]"]
  C6 = Tantalum Capacitor [capacitance=0.05µF package="100 mil [THT, tantalum]"]
  V+_G = Battery block 9V
  ANT = female pin header, 2 pins [form="♀ (female)"]
  OUT = female pin header, 2 pins [form="♀ (female)"]
  POT = female pin header, 3 pins [form="♀ (female)"]

nets:
  N1: LM386.GAIN, C3.-, C3.+
  N2: LM386.+IN, POT.pin2
  N3: LM386.OUT, C2.+, C6.+
  N4: LM386.V+, V1.V+, V+_G.+
  N5: LM386.BP, C5.+
  N6: C2.-, OUT.pin1
  N7: R2.Pin_0, C6.-
  GND: R2.Pin_1
  N8: ANT.pin2, POT.pin1

notes:
  ajouter place batterie
  EMF AMP
  G
